# Fritzing sketch PowerBoard (saved by Fritzing 0.9.3b)
circuit board: 8.46667cm x 5.64444cm
breadboards: 1

parts:
  WeMos_D1_Mini1 = WeMos D1 Mini
  U1 = RELAY [package=relay-jzc]
  U2 = RELAY [package=relay-jzc]
  U3 = RELAY [package=relay-jzc]
  U4 = RELAY [package=relay-jzc]

nets:
  N1: WeMos_D1_Mini1.D1, U4.COIL1
  N2: WeMos_D1_Mini1.D2, U3.COIL1
  N3: WeMos_D1_Mini1.D3, U2.COIL1
  N4: WeMos_D1_Mini1.D4, U1.COIL1
  GND: WeMos_D1_Mini1.G
  N5: U1.COIL2, U2.COIL2, U3.COIL2, U4.COIL2
